# Fritzing sketch emetteur_normal (saved by Fritzing 0.9.2b)
breadboards: 1

parts:
  S1 = Pushbutton [package="[THT]"]
  S2 = Pushbutton [package="[THT]"]
  S3 = Pushbutton [package="[THT]"]
  S4 = Pushbutton [package="[THT]"]
  S5 = Pushbutton [package="[THT]"]
  Composant1 = Arduino Uno (Rev3)
  LED1 = LED - 3mm [color="Red (633nm)" package="3 mm [THT]"]
  R1 = Resistor [tolerance=±5% resistance=100 package="0402 [SMD]"]

nets:
  N1: S1.Pin_1, S1.Pin_2, S2.Pin_1, S2.Pin_2, S3.Pin_1, S3.Pin_2, S4.Pin_1, S4.Pin_2, S5.Pin_1, S5.Pin_2, Composant1.GND, R1.Pin_0
  N2: S1.Pin_3, S1.Pin_4, Composant1.D4
  N3: S2.Pin_3, Composant1.D5_PWM
  N4: S3.Pin_3, Composant1.D6_PWM
  N5: S4.Pin_3, S4.Pin_4, Composant1.D7
  N6: S5.Pin_3, S5.Pin_4, Composant1.D8
  N7: Composant1.D12/MISO, LED1.anode
  N8: LED1.cathode, R1.Pin_1
