# Fritzing sketch emetteur_ruban_led (saved by Fritzing 0.9.2b)
breadboards: 1

parts:
  S1 = Pushbutton [package="[THT]"]
  S2 = Pushbutton [package="[THT]"]
  S3 = Pushbutton [package="[THT]"]
  S4 = Pushbutton [package="[THT]"]
  S5 = Pushbutton [package="[THT]"]
  Composant1 = Arduino Uno (Rev3)
  U2 = Tri-Color LED SMD [package=led-tricolor-smd]

nets:
  GND: S1.Pin_1, S1.Pin_2, S2.Pin_1, S2.Pin_2, S3.Pin_1, S3.Pin_2, S4.Pin_1, S4.Pin_2, S5.Pin_1, S5.Pin_2, Composant1.GND, U2.Gnd
  N1: S1.Pin_3, S1.Pin_4, Composant1.D4
  N2: S2.Pin_3, Composant1.D5_PWM
  N3: S3.Pin_3, Composant1.D6_PWM
  N4: S4.Pin_3, S4.Pin_4, Composant1.D7
  N5: S5.Pin_3, S5.Pin_4, Composant1.D8
  N6: Composant1.D9_PWM, U2.Input
  N7: Composant1.5V, U2.Pwm

custom parts:
  Tri-Color LED SMD: Tri-Color LED SMD Proven layout and schematic for triple color LED in SMD package - common anode. Spark Fun Electronics SKU : COM-07844
