# Fritzing sketch recepteur (saved by Fritzing 0.9.2b)
breadboards: 1

parts:
  J1 = Piezo Speaker
  P1 = S1133 Si Photodiode [package="8mm Ceramic [THT]"]
  Composant1 = Arduino Uno (Rev3)
  R1 = Resistor [tolerance=±5% resistance=220 package="2010 [SMD]"]
  LED1 = smd LED [color="Red (633nm)" package="1206 [SMD]"]
  R2 = Resistor [tolerance=±5% resistance=220 package="2512 [SMD]"]

nets:
  N1: J1.pin1, P1.cathode, Composant1.GND, R2.Pin_0
  N2: J1.pin2, R1.Pin_1
  N3: P1.anode, Composant1.A0
  N4: Composant1.D12/MISO, R1.Pin_0
  N5: Composant1.D7, LED1.anode
  N6: LED1.cathode, R2.Pin_1
